# Fritzing sketch remote_door_lock (saved by Fritzing 0.9.0b)
breadboards: 1

parts:
  부품1 = Arduino Uno (Rev3)
  R1 = Resistor [tolerance=±5% resistance=1k package=THT]
  S1 = Pushbutton [package="[THT]"]
  LED1 = LED - 5mm [color="Green (555nm)" package="5 mm [THT]"]
  R2 = Resistor [tolerance=±5% resistance=1k package=THT]
  Q1 = NPN-Transistor [package="TO92 [THT]"]
  R3 = Resistor [tolerance=±5% resistance=10k package=THT]
  R4 = Resistor [tolerance=±5% resistance=1k package=THT]
  LED2 = LED - 5mm [color="Red (633nm)" package="5 mm [THT]"]

nets:
  N1: 부품1.D2, R1.Pin_0, S1.Pin_3, S1.Pin_4
  N2: 부품1.D4, LED1.anode
  N3: 부품1.D5_PWM, LED2.anode
  N4: 부품1.D7, R3.Pin_1
  N5: 부품1.GND, R1.Pin_1, S1.Pin_1, S1.Pin_2, R2.Pin_0, Q1.C, R4.Pin_1
  N6: LED1.cathode, R2.Pin_1
  N7: Q1.B, R3.Pin_0
  N8: R4.Pin_0, LED2.cathode
